// Logisim project level_handler.circ as structural Verilog: 1 circuit, main circuit main
module main (
  input  lvl1,
  input  lvl2,
  input  lvl3,
  input  lvl4,
  input  [15:0] score,
  input  reset,
  output \output 
);

  wire and_1_out, and_2_out, and_3_out, and_4_out, comparator_1_eq, comparator_2_eq, comparator_3_eq,
       demultiplexer_1_out0, demultiplexer_1_out1, demultiplexer_1_out2, demultiplexer_1_out3, or_1_out;
  wire [1:0] counter_1_q;

  Comparator #(.width(16), .mode("unsigned")) comparator_1 (
    .a(score), .b({16{1'b1}}), .eq(comparator_1_eq));  // open: gt, lt
  Comparator #(.width(16), .mode("unsigned")) comparator_2 (
    .a(score), .b({16{1'b1}}), .eq(comparator_2_eq));  // open: gt, lt
  Comparator #(.width(16), .mode("unsigned")) comparator_3 (
    .a(score), .b({16{1'b1}}), .eq(comparator_3_eq));  // open: gt, lt
  Demultiplexer #(.select(2), .enable("false")) demultiplexer_1 (
    .out0(demultiplexer_1_out0), .out1(demultiplexer_1_out1), .out2(demultiplexer_1_out2),
    .out3(demultiplexer_1_out3), .in(1'b1), .sel(counter_1_q));
  Counter #(.width(2), .max('h3)) counter_1 (
    .Q(counter_1_q), .clk(or_1_out), .clr(reset));  // open: load, D, count, carry
  or or_1 (or_1_out, comparator_1_eq, comparator_2_eq, comparator_3_eq);
  and and_1 (and_1_out, demultiplexer_1_out0, lvl1);
  or or_2 (\output , and_1_out, and_2_out, and_3_out, and_4_out);
  and and_2 (and_2_out, demultiplexer_1_out1, lvl2);
  and and_3 (and_3_out, demultiplexer_1_out2, lvl3);
  and and_4 (and_4_out, demultiplexer_1_out3, lvl4);
endmodule
