// Logisim project student_drop.circ as structural Verilog: 1 circuit, main circuit main
module main (
  input  [31:0] \input ,
  input  catch,
  input  send,
  output [31:0] \output 
);

  wire and_2_out, and_3_out, and_4_out, clock_1_out, nand_1_out, not_1_out, or_1_out, or_2_out, or_3_out;
  wire [4:0] counter_1_q, counter_2_q;
  wire [31:0] and_1_out, multiplexer_1_out, shifter_1_out;

  Multiplexer #(.width(32), .enable("false")) multiplexer_1 (
    .in0({32{1'b0}}), .in1({32{1'b1}}), .out(multiplexer_1_out), .sel(nand_1_out));
  assign and_1_out = \input  & multiplexer_1_out;  // AND_Gate and_1, 32 bits wide
  Counter #(.width(5), .max('h5)) counter_1 (
    .load(1'b1), .Q(counter_1_q), .clk(and_2_out));  // open: D, count, carry, clr
  and and_2 (and_2_out, or_1_out, clock_1_out);
  or or_1 (or_1_out, send, or_2_out);
  Shifter #(.width(32)) shifter_1 (.in(and_1_out), .\dist (counter_1_q), .out(shifter_1_out));
  or or_2 (or_2_out, counter_1_q[0], counter_1_q[1], counter_1_q[2], counter_1_q[3], counter_1_q[4]);
  Clock #(.highDuration(64), .lowDuration(64)) clock_1 (.out(clock_1_out));
  not not_1 (not_1_out, catch);
  and and_3 (and_3_out, ~or_2_out, clock_1_out);  // AND_Gate
  Shifter #(.width(32), .shift("lr")) shifter_2 (.in(shifter_1_out), .\dist (counter_2_q), .out(\output ));
  Counter #(.width(5), .max('h1f)) counter_2 (
    .load(catch), .D({5{1'b1}}), .count(not_1_out), .Q(counter_2_q), .clk(or_3_out));  // open: carry, clr
  or or_3 (or_3_out, catch, send, and_4_out);
  and and_4 (and_4_out, and_3_out, nand_1_out);
  nand nand_1 (nand_1_out, counter_2_q[4], counter_2_q[3], counter_2_q[2], counter_2_q[1], counter_2_q[0]);

  // Notes on the sheet:
  //   w gore
  //   w dol
endmodule
